// Logisim project d_flipflop.circ as structural Verilog: 1 circuit, main circuit main
module main (
  input  Write,
  input  Input,
  output Output
);

  wire nand_1_out, nand_2_out, nand_3_out, nand_4_out, nand_6_out;

  nand nand_1 (nand_1_out, nand_4_out, nand_2_out);
  nand nand_2 (nand_2_out, nand_1_out, Write);
  nand nand_3 (nand_3_out, nand_2_out, Write, nand_4_out);
  nand nand_4 (nand_4_out, nand_3_out, Input);
  nand nand_5 (Output, nand_2_out, nand_6_out);
  nand nand_6 (nand_6_out, Output, nand_3_out);
endmodule
