// Logisim project decoder.circ as structural Verilog: 1 circuit, main circuit main
module main (
  input  in_1,
  input  in_2,
  output D0,
  output D1,
  output D2,
  output D3
);

  wire not_1_out, not_2_out;

  not not_1 (not_1_out, in_2);
  not not_2 (not_2_out, in_1);
  and and_1 (D0, not_1_out, not_2_out);
  and and_2 (D1, not_2_out, in_2);
  and and_3 (D2, not_1_out, in_1);
  and and_4 (D3, in_2, in_1);
endmodule
