// Logisim project register_file.circ as structural Verilog: 7 circuits, main circuit main
module main (
  input  in_1,
  input  in_2,
  input  Enable_write,
  input  A0,
  input  A1,
  input  A2,
  input  A3,
  output O0,
  output O1,
  output O2,
  output O3
);

  wire and_1_out, and_2_out, d_ff_1_q, d_ff_2_q, d_ff_3_q, d_ff_4_q, d_ff_5_q, d_ff_6_q, d_ff_7_q, d_ff_8_q,
       not_1_out;

  not not_1 (not_1_out, in_2);
  and and_1 (and_1_out, Enable_write, not_1_out);
  D_Flip_Flop d_ff_1 (.D(A0), .clk(and_1_out), .Q(d_ff_1_q));  // open: Qn, preset, reset
  D_Flip_Flop d_ff_2 (.D(A1), .clk(and_1_out), .Q(d_ff_2_q));  // open: Qn, preset, reset
  D_Flip_Flop d_ff_3 (.D(A2), .clk(and_1_out), .Q(d_ff_3_q));  // open: Qn, preset, reset
  D_Flip_Flop d_ff_4 (.D(A3), .clk(and_1_out), .Q(d_ff_4_q));  // open: Qn, preset, reset
  and and_2 (and_2_out, Enable_write, in_2);
  D_Flip_Flop d_ff_5 (.D(A0), .clk(and_2_out), .Q(d_ff_5_q));  // open: Qn, preset, reset
  D_Flip_Flop d_ff_6 (.D(A1), .clk(and_2_out), .Q(d_ff_6_q));  // open: Qn, preset, reset
  D_Flip_Flop d_ff_7 (.D(A2), .clk(and_2_out), .Q(d_ff_7_q));  // open: Qn, preset, reset
  D_Flip_Flop d_ff_8 (.D(A3), .clk(and_2_out), .Q(d_ff_8_q));  // open: Qn, preset, reset
  Multiplexer #(.enable("false")) multiplexer_1 (.in0(d_ff_1_q), .in1(d_ff_5_q), .out(O0), .sel(in_1));
  Multiplexer #(.enable("false")) multiplexer_2 (.in0(d_ff_2_q), .in1(d_ff_6_q), .out(O1), .sel(in_1));
  Multiplexer #(.enable("false")) multiplexer_3 (.in0(d_ff_3_q), .in1(d_ff_7_q), .out(O2), .sel(in_1));
  Multiplexer #(.enable("false")) multiplexer_4 (.in0(d_ff_4_q), .in1(d_ff_8_q), .out(O3), .sel(in_1));

  // Notes on the sheet:
  //   Input
  //   Select read register
  //   Select write register
  //   Register 0
  //   Register 1
  //   Multiplexers
  //   Output
endmodule

module reg1 (
  input  A0,
  input  A1,
  input  A2,
  input  A3,
  output O0,
  output O1,
  output O2,
  output O3
);

  wire clock_1_out;

  Clock clock_1 (.out(clock_1_out));
  D_Flip_Flop d_ff_1 (.clk(clock_1_out), .D(A0), .Q(O0));  // open: Qn, preset, reset
  D_Flip_Flop d_ff_2 (.clk(clock_1_out), .D(A1), .Q(O1));  // open: Qn, preset, reset
  D_Flip_Flop d_ff_3 (.clk(clock_1_out), .D(A2), .Q(O2));  // open: Qn, preset, reset
  D_Flip_Flop d_ff_4 (.clk(clock_1_out), .D(A3), .Q(O3));  // open: Qn, preset, reset

  // Notes on the sheet:
  //   Input
  //   Register 0
  //   Output
endmodule

module reg2 (
  input  Enable_write_5bbfcef2,
  input  A0,
  input  A1,
  input  A2,
  input  A3,
  output O0,
  output O1,
  output O2,
  output O3
);

  wire and_1_out, clock_1_out;

  Clock clock_1 (.out(clock_1_out));
  and and_1 (and_1_out, clock_1_out, Enable_write_5bbfcef2);
  D_Flip_Flop d_ff_1 (.clk(and_1_out), .D(A0), .Q(O0));  // open: Qn, preset, reset
  D_Flip_Flop d_ff_2 (.clk(and_1_out), .D(A1), .Q(O1));  // open: Qn, preset, reset
  D_Flip_Flop d_ff_3 (.clk(and_1_out), .D(A2), .Q(O2));  // open: Qn, preset, reset
  D_Flip_Flop d_ff_4 (.clk(and_1_out), .D(A3), .Q(O3));  // open: Qn, preset, reset

  // Notes on the sheet:
  //   Input
  //   Register 0
  //   Output
endmodule

module reg3 (
  input  Enable_write_5bbfcef2,
  input  Select_register_9cb3a1d4,
  input  A0,
  input  A1,
  input  A2,
  input  A3,
  output O0,
  output O1,
  output O2,
  output O3
);

  wire and_1_out, clock_1_out, d_ff_1_q, d_ff_4_q, undriven, undriven_2, undriven_3, undriven_4;

  Clock clock_1 (.out(clock_1_out));
  and and_1 (and_1_out, clock_1_out, Enable_write_5bbfcef2);
  D_Flip_Flop d_ff_1 (.Q(d_ff_1_q), .Qn(d_ff_1_q), .preset(undriven_2), .reset(undriven_3));  // open: D, clk
  D_Flip_Flop d_ff_2 (.Q(d_ff_1_q), .Qn(d_ff_1_q), .preset(undriven_3), .reset(undriven_4));  // open: D, clk
  D_Flip_Flop d_ff_3 (.Q(d_ff_1_q), .Qn(d_ff_1_q), .preset(undriven_4), .reset(d_ff_4_q));  // open: D, clk
  D_Flip_Flop d_ff_4 (.clk(undriven), .D(A3), .Q(d_ff_4_q));  // open: Qn, preset, reset
  D_Flip_Flop d_ff_5 (.clk(d_ff_1_q));  // open: D, Q, Qn, preset, reset
  D_Flip_Flop d_ff_6 (.clk(d_ff_1_q));  // open: D, Q, Qn, preset, reset
  D_Flip_Flop d_ff_7 (.clk(d_ff_1_q));  // open: D, Q, Qn, preset, reset
  D_Flip_Flop d_ff_8 (.clk(d_ff_1_q));  // open: D, Q, Qn, preset, reset

  // Notes on the sheet:
  //   Input
  //   Register 0
  //   Register 1
  //   Output
endmodule

module reg4 (
  input  Enable_write_5bbfcef2,
  input  Select_register_9cb3a1d4,
  input  A0,
  input  A1,
  input  A2,
  input  A3,
  output O0,
  output O1,
  output O2,
  output O3
);

  wire and_1_out, clock_1_out, d_ff_1_q, d_ff_4_q, d_ff_5_q, d_ff_6_q, d_ff_7_q, d_ff_8_q, undriven,
       undriven_2, undriven_3, undriven_4;

  Clock clock_1 (.out(clock_1_out));
  and and_1 (and_1_out, clock_1_out, Enable_write_5bbfcef2);
  D_Flip_Flop d_ff_1 (.Q(d_ff_1_q), .Qn(d_ff_1_q), .preset(undriven_2), .reset(undriven_3));  // open: D, clk
  D_Flip_Flop d_ff_2 (.Q(d_ff_1_q), .Qn(d_ff_1_q), .preset(undriven_3), .reset(undriven_4));  // open: D, clk
  D_Flip_Flop d_ff_3 (.Q(d_ff_1_q), .Qn(d_ff_1_q), .preset(undriven_4), .reset(d_ff_4_q));  // open: D, clk
  D_Flip_Flop d_ff_4 (.clk(undriven), .D(A3), .Q(d_ff_4_q));  // open: Qn, preset, reset
  D_Flip_Flop d_ff_5 (.clk(d_ff_1_q), .Q(d_ff_5_q));  // open: D, Qn, preset, reset
  D_Flip_Flop d_ff_6 (.clk(d_ff_1_q), .Q(d_ff_6_q));  // open: D, Qn, preset, reset
  D_Flip_Flop d_ff_7 (.clk(d_ff_1_q), .Q(d_ff_7_q));  // open: D, Qn, preset, reset
  D_Flip_Flop d_ff_8 (.clk(d_ff_1_q), .Q(d_ff_8_q));  // open: D, Qn, preset, reset
  Multiplexer #(.enable("false")) multiplexer_1 (
    .in0(undriven_2), .in1(d_ff_5_q), .out(O0), .sel(Select_register_9cb3a1d4));
  Multiplexer #(.enable("false")) multiplexer_2 (
    .in0(undriven_3), .in1(d_ff_6_q), .out(O1), .sel(Select_register_9cb3a1d4));
  Multiplexer #(.enable("false")) multiplexer_3 (
    .in0(undriven_4), .in1(d_ff_7_q), .out(O2), .sel(Select_register_9cb3a1d4));
  Multiplexer #(.enable("false")) multiplexer_4 (
    .in0(d_ff_4_q), .in1(d_ff_8_q), .out(O3), .sel(Select_register_9cb3a1d4));

  // Notes on the sheet:
  //   Input
  //   Register 0
  //   Register 1
  //   Multiplexers
  //   Output
endmodule

module reg5 (
  input  Enable_write_d7aaa99e,
  input  Select_register_9cb3a1d4,
  input  A0,
  input  A1,
  input  A2,
  input  A3,
  output O0,
  output O1,
  output O2,
  output O3
);

  wire and_1_out, clock_1_out, d_ff_1_q, d_ff_4_q, d_ff_5_q, d_ff_6_q, d_ff_7_q, d_ff_8_q,
       demultiplexer_1_out0, undriven, undriven_2, undriven_3;

  Clock clock_1 (.out(clock_1_out));
  and and_1 (and_1_out, clock_1_out, Enable_write_d7aaa99e);
  D_Flip_Flop d_ff_1 (.Q(d_ff_1_q), .Qn(d_ff_1_q), .preset(undriven), .reset(undriven_2));  // open: D, clk
  D_Flip_Flop d_ff_2 (.Q(d_ff_1_q), .Qn(d_ff_1_q), .preset(undriven_2), .reset(undriven_3));  // open: D, clk
  D_Flip_Flop d_ff_3 (.Q(d_ff_1_q), .Qn(d_ff_1_q), .preset(undriven_3), .reset(d_ff_4_q));  // open: D, clk
  D_Flip_Flop d_ff_4 (.clk(demultiplexer_1_out0), .D(A3), .Q(d_ff_4_q));  // open: Qn, preset, reset
  Demultiplexer #(.enable("false")) demultiplexer_1 (
    .out0(demultiplexer_1_out0), .out1(d_ff_1_q), .in(and_1_out), .sel(Select_register_9cb3a1d4));
  D_Flip_Flop d_ff_5 (.clk(d_ff_1_q), .D(A0), .Q(d_ff_5_q));  // open: Qn, preset, reset
  D_Flip_Flop d_ff_6 (.clk(d_ff_1_q), .D(A1), .Q(d_ff_6_q));  // open: Qn, preset, reset
  D_Flip_Flop d_ff_7 (.clk(d_ff_1_q), .D(A2), .Q(d_ff_7_q));  // open: Qn, preset, reset
  D_Flip_Flop d_ff_8 (.clk(d_ff_1_q), .D(A3), .Q(d_ff_8_q));  // open: Qn, preset, reset
  Multiplexer #(.enable("false")) multiplexer_1 (
    .in0(undriven), .in1(d_ff_5_q), .out(O0), .sel(Select_register_9cb3a1d4));
  Multiplexer #(.enable("false")) multiplexer_2 (
    .in0(undriven_2), .in1(d_ff_6_q), .out(O1), .sel(Select_register_9cb3a1d4));
  Multiplexer #(.enable("false")) multiplexer_3 (
    .in0(undriven_3), .in1(d_ff_7_q), .out(O2), .sel(Select_register_9cb3a1d4));
  Multiplexer #(.enable("false")) multiplexer_4 (
    .in0(d_ff_4_q), .in1(d_ff_8_q), .out(O3), .sel(Select_register_9cb3a1d4));

  // Notes on the sheet:
  //   Input
  //   Register 0
  //   Demultiplexer
  //   Register 1
  //   Multiplexers
  //   Output
endmodule

module reg_rw (
  input  [1:0] Select_read_20ae2d32,
  input  [1:0] Select_write_bb9d4264,
  output O0,
  output O1,
  output O2,
  output O3
);

  wire clock_1_out, d_ff_1_q, d_ff_2_q, d_ff_3_q, d_ff_4_q, d_ff_5_q, d_ff_6_q, d_ff_7_q, d_ff_8_q, d_ff_9_q,
       d_ff_10_q, d_ff_11_q, d_ff_12_q, demultiplexer_1_out0, demultiplexer_1_out1, demultiplexer_1_out2,
       nand_1_out;
  wire [3:0] controlled_buffer_1_out;

  Clock clock_1 (.out(clock_1_out));
  D_Flip_Flop d_ff_1 (
    .clk(demultiplexer_1_out0), .D(controlled_buffer_1_out[0]), .Q(d_ff_1_q));  // open: Qn, preset, reset
  D_Flip_Flop d_ff_2 (
    .clk(demultiplexer_1_out0), .D(controlled_buffer_1_out[1]), .Q(d_ff_2_q));  // open: Qn, preset, reset
  D_Flip_Flop d_ff_3 (
    .clk(demultiplexer_1_out0), .D(controlled_buffer_1_out[2]), .Q(d_ff_3_q));  // open: Qn, preset, reset
  D_Flip_Flop d_ff_4 (
    .clk(demultiplexer_1_out0), .D(controlled_buffer_1_out[3]), .Q(d_ff_4_q));  // open: Qn, preset, reset
  Demultiplexer #(.select(2), .enable("false")) demultiplexer_1 (
    .out0(demultiplexer_1_out0), .out1(demultiplexer_1_out1), .out2(demultiplexer_1_out2), .in(clock_1_out),
    .sel(Select_write_bb9d4264));  // open: out3
  D_Flip_Flop d_ff_5 (
    .clk(demultiplexer_1_out1), .D(controlled_buffer_1_out[0]), .Q(d_ff_5_q));  // open: Qn, preset, reset
  D_Flip_Flop d_ff_6 (
    .clk(demultiplexer_1_out1), .D(controlled_buffer_1_out[1]), .Q(d_ff_6_q));  // open: Qn, preset, reset
  D_Flip_Flop d_ff_7 (
    .clk(demultiplexer_1_out1), .D(controlled_buffer_1_out[2]), .Q(d_ff_7_q));  // open: Qn, preset, reset
  D_Flip_Flop d_ff_8 (
    .clk(demultiplexer_1_out1), .D(controlled_buffer_1_out[3]), .Q(d_ff_8_q));  // open: Qn, preset, reset
  D_Flip_Flop d_ff_9 (
    .clk(demultiplexer_1_out2), .D(controlled_buffer_1_out[0]), .Q(d_ff_9_q));  // open: Qn, preset, reset
  D_Flip_Flop d_ff_10 (
    .clk(demultiplexer_1_out2), .D(controlled_buffer_1_out[1]), .Q(d_ff_10_q));  // open: Qn, preset, reset
  D_Flip_Flop d_ff_11 (
    .clk(demultiplexer_1_out2), .D(controlled_buffer_1_out[2]), .Q(d_ff_11_q));  // open: Qn, preset, reset
  D_Flip_Flop d_ff_12 (
    .clk(demultiplexer_1_out2), .D(controlled_buffer_1_out[3]), .Q(d_ff_12_q));  // open: Qn, preset, reset
  Multiplexer #(.select(2), .enable("false")) multiplexer_1 (
    .in0(d_ff_1_q), .in1(d_ff_5_q), .in2(d_ff_9_q), .in3(1'b0), .out(O0), .sel(Select_read_20ae2d32));
  Multiplexer #(.select(2), .enable("false")) multiplexer_2 (
    .in0(d_ff_2_q), .in1(d_ff_6_q), .in2(d_ff_10_q), .in3(1'b0), .out(O1), .sel(Select_read_20ae2d32));
  Multiplexer #(.select(2), .enable("false")) multiplexer_3 (
    .in0(d_ff_3_q), .in1(d_ff_7_q), .in2(d_ff_11_q), .in3(1'b0), .out(O2), .sel(Select_read_20ae2d32));
  Multiplexer #(.select(2), .enable("false")) multiplexer_4 (
    .in0(d_ff_4_q), .in1(d_ff_8_q), .in2(d_ff_12_q), .in3(1'b0), .out(O3), .sel(Select_read_20ae2d32));
  nand nand_1 (nand_1_out, Select_read_20ae2d32[0], Select_read_20ae2d32[1]);
  assign controlled_buffer_1_out = nand_1_out ? {O3, O2, O1, O0} : 4'bz;  // Controlled_Buffer controlled_buffer_1

  // Notes on the sheet:
  //   Register 0
  //   Demultiplexer
  //   Register 1
  //   Register 2
  //   Multiplexers
  //   Output
  //   Bus
endmodule
