// Logisim project ripple_carry_adder.circ as structural Verilog: 1 circuit, main circuit main
module main (
  input  in_1,
  input  in_2,
  input  in_3,
  input  B,
  input  in_5,
  input  in_6,
  input  in_7,
  output carry_out,
  output out_9,
  output out_10,
  output out_11
);

  wire and_1_out, and_2_out, and_3_out, and_4_out, and_5_out, and_6_out, or_2_out, or_3_out, xor_1_out,
       xor_3_out, xor_5_out;

  or or_1 (carry_out, and_1_out, and_2_out);
  and and_1 (and_1_out, B, in_1);
  and and_2 (and_2_out, xor_1_out, or_2_out);
  xor xor_1 (xor_1_out, B, in_1);
  xor xor_2 (out_9, xor_1_out, or_2_out);
  or or_2 (or_2_out, and_3_out, and_4_out);
  and and_3 (and_3_out, in_5, in_2);
  and and_4 (and_4_out, xor_3_out, or_3_out);
  xor xor_3 (xor_3_out, in_5, in_2);
  xor xor_4 (out_10, xor_3_out, or_3_out);
  or or_3 (or_3_out, and_5_out, and_6_out);
  and and_5 (and_5_out, in_6, in_3);
  and and_6 (and_6_out, xor_5_out, in_7);
  xor xor_5 (xor_5_out, in_6, in_3);
  xor xor_6 (out_11, xor_5_out, in_7);

  // Notes on the sheet:
  //   3-bit A
  //   3-bit B
  //   ------------
  //   3-bit C with carry-out
  //   A
  //   C
endmodule
