// Logisim project alu.circ as structural Verilog: 1 circuit, main circuit main
module main (
  input  [3:0] A,
  input  [3:0] B,
  input  [1:0] opcode,
  output [3:0] out_4
);

  wire [1:0] comparator_1_gt;
  wire [3:0] adder_1_out, adder_2_out, adder_3_out, negator_1_out;

  Negator #(.width(4)) negator_1 (.in(B), .out(negator_1_out));
  Comparator #(.width(4)) comparator_1 (
    .a(A), .b(4'b0000), .gt(comparator_1_gt[0]), .lt(comparator_1_gt[1]));  // open: eq
  Adder #(.width(4)) adder_1 (.a(A), .b(B), .out(adder_1_out));  // open: cin, cout
  Adder #(.width(4)) adder_2 (.a(A), .b(negator_1_out), .out(adder_2_out));  // open: cin, cout
  Adder #(.width(4)) adder_3 (.a(A), .b(4'b0001), .out(adder_3_out));  // open: cin, cout
  Multiplexer #(.select(2), .width(4), .enable("false")) multiplexer_1 (
    .in0(adder_1_out), .in1(adder_2_out), .in2(adder_3_out), .in3({2'b00, comparator_1_gt}), .out(out_4),
    .sel(opcode));
endmodule
